# Fritzing sketch Placa Central VF (saved by Fritzing 0.9.3b)
circuit board: 8.6cm x 8cm

parts:
  Arduino_Nano = Arduino Nano (Rev3.0)
  SA1-[3] = RJ9 [package=rj9]
  SD1-[1] = RJ9 [package=rj9]
  SD2-[2] = RJ9 [package=rj9]
  SA2-[4] = RJ9 [package=rj9]
  Motor_B = female pin header, 2 pins [form="♀ (female)"]
  Conector_P4 = Power plug
  Motor_A = female pin header, 2 pins [form="♀ (female)"]
  Driver = Motor Driver 1A Dual TB6612FNG
  R1 = Resistor [tolerance=±5% resistance=10k package=THT]
  Chave = Pushbutton [package="[THT]"]
  Buzzer = Buzzer 12mm [package=buzzer-12mm-ns-kit]
  C4 = Electrolytic Capacitor [capacitance=470µF voltage=16V package="200 mil [THT, electrolytic]"]
  Jumper = male pin header, 2 pins [form="♂ (male)"]
  Chave_Geral = female pin header, 2 pins [form="♀ (female)"]

nets:
  GND: Arduino_Nano.GND, SA1-[3].2, SD1-[1].2, SD2-[2].2, SA2-[4].2, Conector_P4.GND, Driver.GND, R1.Pin_1, Buzzer.2, C4.-
  N1: Arduino_Nano.D2, Driver.BIN1
  N2: Arduino_Nano.D3, Driver.AIN1
  N3: Arduino_Nano.D4, SD2-[2].4
  N4: Arduino_Nano.D5, SD2-[2].1
  N5: Arduino_Nano.D6, Driver.AIN2
  N6: Arduino_Nano.D7, SD1-[1].4
  N7: Arduino_Nano.D8, SD1-[1].1
  N8: Arduino_Nano.D9, Buzzer.1
  N9: Arduino_Nano.D10, Driver.PWMB
  N10: Arduino_Nano.D11/MOSI, Driver.PWMA
  N11: Arduino_Nano.D12/MISO, Driver.BIN2
  N12: Arduino_Nano.VIN, Driver.VM, C4.+, Chave_Geral.pin2
  5V: Arduino_Nano.5V, SA1-[3].3, SD1-[1].3, SD2-[2].3, SA2-[4].3, Driver.VCC, Chave.Pin_3, Chave.Pin_4
  N13: Arduino_Nano.A7, R1.Pin_0, Chave.Pin_1, Chave.Pin_2
  N14: Arduino_Nano.A5, SA2-[4].4
  N15: Arduino_Nano.A4, SA2-[4].1
  N16: Arduino_Nano.A3, SA1-[3].4
  N17: Arduino_Nano.A2, SA1-[3].1
  N18: Arduino_Nano.D13/SCK, Jumper.pin2
  N19: Motor_B.pin1, Driver.B01
  N20: Motor_B.pin2, Driver.B02
  N21: Conector_P4.VCC, Chave_Geral.pin1
  N22: Motor_A.pin1, Driver.A01
  N23: Motor_A.pin2, Driver.A02
  N24: Driver.STBY, Jumper.pin1
