# Fritzing sketch Placa Toque VF (saved by Fritzing 0.9.3b)
circuit board: 3.78777cm x 1.93411cm
breadboards: 1

parts:
  J1 = RJ9 [package=rj9]
  R1 = Resistor [tolerance=±5% resistance=10k package=THT]
  R2 = Resistor [tolerance=±5% resistance=10k package=THT]
  Chave_Esquerda = SWITCH-MOMENTARY-2 [package=tactile-switch-1101ne]
  Chave_Direita = SWITCH-MOMENTARY-2 [package=tactile-switch-1101ne]

nets:
  N1: J1.1, R1.Pin_0, Chave_Direita.1
  GND: J1.2, R1.Pin_1, R2.Pin_1
  5V: J1.3, Chave_Esquerda.2, Chave_Direita.2
  N2: J1.4, R2.Pin_0, Chave_Esquerda.1
