# Fritzing sketch Placa US VF (saved by Fritzing 0.9.3b)
circuit board: 2.5cm x 4cm
breadboards: 1

parts:
  hc-sr2 = hc-sr04
  J1 = RJ9 [package=rj9]

nets:
  N1: hc-sr2.VCC, J1.3
  N2: hc-sr2.Trig, J1.4
  N3: hc-sr2.Echo, J1.1
  N4: hc-sr2.GND, J1.2
