# Fritzing sketch Placa da IMU VF (saved by Fritzing 0.9.3b)
circuit board: 3.71cm x 3cm
breadboards: 1

parts:
  J1 = RJ9 [package=rj9]
  MPU-6050 = MPU-6050 GY-521 [form="♀ (female)"]

nets:
  N1: J1.1, MPU-6050.connector3
  N2: J1.2, MPU-6050.connector1
  N3: J1.3, MPU-6050.connector0
  N4: J1.4, MPU-6050.connector2
