# Fritzing sketch Placa do IR VF (saved by Fritzing 0.9.3b)
circuit board: 5cm x 2cm
breadboards: 1

parts:
  IR-Direita = male pin header, 4 pins [form="♂ (male)"]
  IR_Esquerda = male pin header, 4 pins [form="♂ (male)"]
  J2 = RJ9 [package=rj9]

nets:
  VCC: IR-Direita.pin1, IR_Esquerda.pin1, J2.3
  GND: IR-Direita.pin2, IR_Esquerda.pin2, J2.2
  ADC - D: IR-Direita.pin4, J2.1
  ADC - E: IR_Esquerda.pin4, J2.4
